# Fritzing sketch Orange Pi Smart Heating & Lighting Project Frtizing File (saved by Fritzing 0.9.3b)
breadboards: 1

parts:
  Lux_Sensor = Adafruit BH1750 [part_number="Adafruit #4681"]
  Relay = Module 4 Relais 5V [package="Module 4 Relais 5V"]
  LED1 = LED - 5mm [color="Red (633nm)" package="5 mm [THT]"]
  R0 = Resistor [tolerance=±5% resistance=220 package=THT]
  Pot_Temp = POT [package=pot_mammoth]
  Pot_Light = POT [package=pot_mammoth]
  R3 = Resistor [tolerance=±5% resistance=100 package=THT]
  R2 = Resistor [tolerance=±5% resistance=100 package=THT]
  R1 = Resistor [tolerance=±5% resistance=100 package=THT]
  R4 = Resistor [tolerance=±5% resistance=100 package=THT]
  Opi = Orange PI 3 LTS
  ADC = MCP3008 8-channel 10-bit ADC [part_number=MCP3008]
  Temp_Sensor = Adafruit BMP280 [part_number="Adafruit #2651"]

nets:
  GND: Lux_Sensor.GND, Relay.GND, Relay.K1-Com, LED1.cathode, Pot_Temp.E, Pot_Light.E, Opi.Pin_4, Opi.Pin_11, Opi.Pin_14, Opi.Pin_22, ADC.Dgnd, ADC.Agnd, Temp_Sensor.GND
  VCC: Lux_Sensor.VCC, Pot_Temp.S, Pot_Light.S, R3.Pin_1, R2.Pin_1, R1.Pin_1, R4.Pin_1, Opi.Pin_26, ADC.Vref, ADC.Vdd, Temp_Sensor.VCC
  N1: Lux_Sensor.SCL, Opi.Pin_24, Temp_Sensor.SCK/SCL
  N2: Lux_Sensor.SDA, Opi.Pin_25, Temp_Sensor.SDI/SDA
  N3: Relay.VCC, Opi.Pin_12
  N4: Relay.IN1, Opi.Pin_10
  N5: Relay.K1-NO, R3.Pin_0, R2.Pin_0, R1.Pin_0, R4.Pin_0
  N6: LED1.anode, R0.Pin_0
  N7: R0.Pin_1, Opi.Pin_23
  N8: Pot_Temp.A, ADC.CH0
  N9: Pot_Light.A, ADC.CH1
  N10: Opi.Pin_2, ADC.CS/shdn
  N11: Opi.Pin_15, ADC.CLK
  N12: Opi.Pin_16, ADC.Dout
  N13: Opi.Pin_17, ADC.Din

custom parts:
  Adafruit BH1750: This is the BH1750 16-bit Ambient Light sensor from Rohm. Because of how important it is to humans and most other living things, sensing the amount of light in an environment is a common place to get started when learning to work with microcontrollers and sensors. Should we turn up the brightness of our display or dim it to save power? Which direction should your robot move to stay in an area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
  Module 4 Relais 5V: Module 4 Relais 5V 4x SPD-06VDC-SD-C
  Orange PI 3 LTS: Orange Pi 3 LTS is an open-source single-board computer with dual-band wireless WiFi and Bluetooth 5.0 .It is highly compact with a dimension of 56X85mm.
  Adafruit BMP280: Bosch has stepped up their game with their new BMP280 sensor, an environmental sensor with temperature, barometric pressure that is the next generation upgrade to the BMP085/BMP180/BMP183. This sensor is great for all sorts of weather sensing and can even be used in both I2C and SPI! This precision sensor from Bosch is the best low-cost, precision sensing solution for measuring barometric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
